// Logisim project crc.circ as structural Verilog: 2 circuits, main circuit CRC
module CRC (
  input  [7:0] in_1,
  input  [3:0] in_2,
  output [10:0] out_3
);

  wire bitfinder_1_found;
  wire [1:0] bitfinder_1_index;
  wire [3:0] bit_extender_2_out, multiplexer_1_out;
  wire [10:0] bit_extender_1_out, shifter_1_out;

  assign bit_extender_1_out = {{3{1'b0}}, in_1};  // Bit_Extender bit_extender_1
  BitFinder #(.width(4), .\type ("high1")) bitfinder_1 (
    .in(in_2), .index(bitfinder_1_index), .found(bitfinder_1_found));
  assign bit_extender_2_out = {{2{1'b0}}, bitfinder_1_index};  // Bit_Extender bit_extender_2
  Multiplexer #(.width(4), .enable("false")) multiplexer_1 (
    .in0(4'b0000), .in1(in_2), .out(multiplexer_1_out), .sel(bitfinder_1_found));
  Shifter #(.width(11)) shifter_1 (.in(bit_extender_1_out), .\dist (bit_extender_2_out), .out(shifter_1_out));
  mod2divider mod2divider_1 (.in_1(shifter_1_out), .in_2(multiplexer_1_out), .out_3(out_3[2:0]));
  // Probe on {in_1, out_3[2:0]}

  assign out_3[10:3] = in_1;

  // Notes on the sheet:
  //   把这个除法器换成模二除法器
endmodule

module mod2divider (
  input  [10:0] in_1,
  input  [3:0] in_2,
  output [2:0] out_3
);

  wire [2:0] multiplexer_5_out, multiplexer_6_out, multiplexer_7_out, multiplexer_8_out;
  wire [3:0] xor_1_out, xor_2_out, xor_3_out, xor_4_out, xor_5_out, xor_6_out, xor_7_out, xor_8_out;
  wire [3:1] multiplexer_2_out, multiplexer_3_out, multiplexer_4_out;

  assign xor_1_out = in_2 ^ {multiplexer_2_out, in_1[0]};  // XOR_Gate xor_1, 4 bits wide
  assign xor_2_out = in_1[10:7] ^ in_2;  // XOR_Gate xor_2, 4 bits wide
  assign xor_3_out = in_2 ^ {multiplexer_3_out, in_1[1]};  // XOR_Gate xor_3, 4 bits wide
  assign xor_4_out = in_2 ^ {multiplexer_4_out, in_1[2]};  // XOR_Gate xor_4, 4 bits wide
  assign xor_5_out = in_2 ^ {multiplexer_6_out, in_1[3]};  // XOR_Gate xor_5, 4 bits wide
  Multiplexer #(.width(3), .enable("false")) multiplexer_1 (
    .in0(xor_1_out[2:0]), .in1({multiplexer_2_out[2:1], in_1[0]}), .out(out_3), .sel(xor_1_out[3]));
  Multiplexer #(.width(3), .enable("false")) multiplexer_2 (
    .in0(xor_3_out[2:0]), .in1({multiplexer_3_out[2:1], in_1[1]}), .out(multiplexer_2_out), .sel(xor_3_out[3]));
  Multiplexer #(.width(3), .enable("false")) multiplexer_3 (
    .in0(xor_4_out[2:0]), .in1({multiplexer_4_out[2:1], in_1[2]}), .out(multiplexer_3_out), .sel(xor_4_out[3]));
  Multiplexer #(.width(3), .enable("false")) multiplexer_4 (
    .in0(xor_5_out[2:0]), .in1({multiplexer_6_out[1:0], in_1[3]}), .out(multiplexer_4_out), .sel(xor_5_out[3]));
  assign xor_6_out = in_2 ^ {multiplexer_8_out, in_1[4]};  // XOR_Gate xor_6, 4 bits wide
  assign xor_7_out = in_2 ^ {multiplexer_7_out, in_1[5]};  // XOR_Gate xor_7, 4 bits wide
  assign xor_8_out = in_2 ^ {multiplexer_5_out, in_1[6]};  // XOR_Gate xor_8, 4 bits wide
  Multiplexer #(.width(3), .enable("false")) multiplexer_5 (
    .in0(xor_2_out[2:0]), .in1(in_1[9:7]), .out(multiplexer_5_out), .sel(xor_2_out[3]));
  Multiplexer #(.width(3), .enable("false")) multiplexer_6 (
    .in0(xor_6_out[2:0]), .in1({multiplexer_8_out[1:0], in_1[4]}), .out(multiplexer_6_out), .sel(xor_6_out[3]));
  Multiplexer #(.width(3), .enable("false")) multiplexer_7 (
    .in0(xor_8_out[2:0]), .in1({multiplexer_5_out[1:0], in_1[6]}), .out(multiplexer_7_out), .sel(xor_8_out[3]));
  Multiplexer #(.width(3), .enable("false")) multiplexer_8 (
    .in0(xor_7_out[2:0]), .in1({multiplexer_7_out[1:0], in_1[5]}), .out(multiplexer_8_out), .sel(xor_7_out[3]));

  // Other names for the same wires on the sheet: divider[3:0] = in_2
endmodule
