// Logisim project fsm.circ as structural Verilog: 4 circuits, main circuit fsm
module fsm (
  input  [1:0] \input ,
  input  clr,
  output out_3
);

  wire clock_1_out;
  wire [2:0] multiplexer_1_out, nextstate_1_n_state0, register_1_q;

  nextState nextstate_1 (
    .state0(register_1_q[2]), .state1(register_1_q[1]), .state2(register_1_q[0]), .in0(\input [1]),
    .in1(\input [0]), .n_state2(nextstate_1_n_state0[2]), .n_state1(nextstate_1_n_state0[1]),
    .n_state0(nextstate_1_n_state0[0]));
  Multiplexer #(.width(3), .enable("false")) multiplexer_1 (
    .in0(nextstate_1_n_state0), .in1(3'b000), .out(multiplexer_1_out), .sel(clr));
  Register #(.width(3)) register_1 (.D(multiplexer_1_out), .Q(register_1_q), .clk(clock_1_out));  // open: en, clr
  Clock clock_1 (.out(clock_1_out));
  outputLogic outputlogic_1 (.curState(register_1_q), .in_2(\input ), .out_3(out_3));

  // Other names for the same wires on the sheet: clear = clr

  // Notes on the sheet:
  //   a = 00
  //   b = 01
  //   c = 10
endmodule

module nextState (
  input  state0,
  input  state1,
  input  state2,
  input  in0,
  input  in1,
  output n_state2,
  output n_state1,
  output n_state0
);

  wire and_1_out, and_2_out, and_3_out, and_4_out, not_1_out, not_2_out, not_3_out, not_4_out, not_5_out,
       not_6_out, not_7_out, not_8_out, not_9_out, not_10_out, not_11_out;

  not not_1 (not_1_out, state0);
  not not_2 (not_2_out, state1);
  not not_3 (not_3_out, in1);
  not not_4 (not_4_out, state0);
  not not_5 (not_5_out, state2);
  not not_6 (not_6_out, in1);
  not not_7 (not_7_out, state0);
  not not_8 (not_8_out, in0);
  not not_9 (not_9_out, state0);
  not not_10 (not_10_out, state2);
  not not_11 (not_11_out, in1);
  and and_1 (and_1_out, not_1_out, not_2_out, state2, not_3_out);
  and and_2 (and_2_out, not_4_out, state1, not_5_out, not_6_out);
  and and_3 (and_3_out, not_7_out, not_8_out, in1);
  and and_4 (and_4_out, not_9_out, state1, not_10_out, not_11_out);
  or or_1 (n_state1, and_1_out, and_2_out);
  or or_2 (n_state0, and_3_out, and_4_out);

  assign n_state2 = 1'b0;
endmodule

module outputLogic (
  input  [2:0] curState,
  input  [1:0] in_2,
  output out_3
);

  wire comparator_1_eq, comparator_2_eq, comparator_3_eq, or_1_out;

  Comparator #(.width(3), .mode("unsigned")) comparator_1 (
    .a(curState), .b(3'b010), .eq(comparator_1_eq));  // open: gt, lt
  Comparator #(.width(2), .mode("unsigned")) comparator_2 (.a(in_2), .b(2'b00), .eq(comparator_2_eq));  // open: gt, lt
  Comparator #(.width(2), .mode("unsigned")) comparator_3 (.a(2'b10), .b(in_2), .eq(comparator_3_eq));  // open: gt, lt
  or or_1 (or_1_out, comparator_2_eq, comparator_3_eq);
  and and_1 (out_3, comparator_1_eq, or_1_out);
endmodule

module test (
  input  reset,
  output halt,
  output out_3
);

  wire clock_1_out;
  wire [1:0] rom_1_data;
  wire [7:0] counter_1_q;

  Counter counter_1 (.Q(counter_1_q), .carry(halt), .clk(clock_1_out), .clr(reset));  // open: load, D, count
  Clock clock_1 (.out(clock_1_out));
  // Probe on rom_1_data
  ROM #(.dataWidth(2)) rom_1 (.addr(counter_1_q), .data(rom_1_data));  // open: sel
  fsm fsm_1 (.\input (rom_1_data), .clr(reset), .out_3(out_3));

  // Notes on the sheet:
  //   contents of rom_1 (hex, n*v repeats v):
  //   0 1 0 2 1 0 1 0 0 0 1 1
endmodule
