// Logisim project ftoi.circ as structural Verilog: 2 circuits, main circuit ftoi
module ftoi (
  input  [15:0] float,
  output [31:0] \integer 
);

  wire comparator_1_eq, comparator_2_eq, comparator_3_eq, comparator_3_gt, comparator_3_lt, comparator_4_lt,
       or_1_out;
  wire [1:0] coder_1_x;
  wire [4:0] negator_2_out, subtractor_1_out, subtractor_2_out;
  wire [31:0] bit_extender_1_out, frac, multiplexer_1_out, negator_1_out, out, shifter_1_out, shifter_2_out;

  Comparator #(.width(5), .mode("unsigned")) comparator_1 (
    .a(float[14:10]), .b({5{1'b0}}), .eq(comparator_1_eq));  // open: gt, lt
  Comparator #(.width(5), .mode("unsigned")) comparator_2 (
    .a(float[14:10]), .b({5{1'b1}}), .eq(comparator_2_eq));  // open: gt, lt
  // Probe on multiplexer_1_out
  Subtractor #(.width(5)) subtractor_1 (.a(float[14:10]), .b(5'b01111), .out(subtractor_1_out));  // open: bin, bout
  or or_1 (or_1_out, comparator_1_eq, comparator_2_eq);
  // Probe on {1'b1, float[9:0]}
  Comparator #(.width(5)) comparator_3 (
    .a(subtractor_1_out), .b({5{1'b0}}), .gt(comparator_3_gt), .eq(comparator_3_eq), .lt(comparator_3_lt));
  Multiplexer #(.width(32), .enable("false")) multiplexer_1 (
    .in0(out), .in1({32{1'b0}}), .out(multiplexer_1_out), .sel(or_1_out));
  coder coder_1 (.a(comparator_3_gt), .b(comparator_3_eq), .c(comparator_3_lt), .x(coder_1_x[0]), .y(coder_1_x[1]));
  Multiplexer #(.width(32), .enable("false")) multiplexer_2 (
    .in0(multiplexer_1_out), .in1(negator_1_out), .out(\integer ), .sel(float[15]));
  Negator #(.width(32)) negator_1 (.in(multiplexer_1_out), .out(negator_1_out));
  // Probe on \integer 
  assign bit_extender_1_out = {{21{1'b0}}, {1'b1, float[9:0]}};  // Bit_Extender bit_extender_1
  Subtractor #(.width(5)) subtractor_2 (.a(5'b01010), .b(subtractor_1_out), .out(subtractor_2_out));  // open: bin, bout
  Shifter #(.width(32), .shift("lr")) shifter_1 (
    .in(bit_extender_1_out), .\dist (subtractor_2_out), .out(shifter_1_out));
  Negator #(.width(5)) negator_2 (.in(subtractor_2_out), .out(negator_2_out));
  Multiplexer #(.select(2), .width(32)) multiplexer_3 (
    .in0({32{1'b0}}), .in1(32'h1), .in2(frac), .out(out), .sel(coder_1_x));  // open: in3, en
  Shifter #(.width(32)) shifter_2 (.in(bit_extender_1_out), .\dist (negator_2_out), .out(shifter_2_out));
  Multiplexer #(.width(32), .enable("false")) multiplexer_4 (
    .in0(shifter_1_out), .in1(shifter_2_out), .out(frac), .sel(comparator_4_lt));
  Comparator #(.width(5)) comparator_4 (.a(subtractor_2_out), .b({5{1'b0}}), .lt(comparator_4_lt));  // open: gt, eq
  // Probe on shifter_2_out

  // Other names for the same wires on the sheet: fraction[9:0] = float[9:0]; exponext[4:0] = float[14:10];
  //   sign = float[15]
endmodule

module coder (
  input  a,
  input  b,
  input  c,
  output x,
  output y
);

  wire not_1_out;

  not not_1 (not_1_out, b);
  and and_1 (y, a, not_1_out);

  assign x = b;
endmodule
