// Logisim project navigaton.circ as structural Verilog: 4 circuits, main circuit navigation
module navigation (
  input  [1:0] dir,
  input  clk,
  input  reset,
  output arrive,
  output hit
);

  wire [2:0] nextstatelogic_1_nstate2, register_1_q;

  nextStateLogic nextstatelogic_1 (
    .state0(register_1_q[2]), .state1(register_1_q[1]), .state2(register_1_q[0]), .in0(dir[1]), .in1(dir[0]),
    .nState0(nextstatelogic_1_nstate2[2]), .nState1(nextstatelogic_1_nstate2[1]),
    .nState2(nextstatelogic_1_nstate2[0]));
  Register #(.width(3)) register_1 (
    .D(nextstatelogic_1_nstate2), .Q(register_1_q), .clk(clk), .clr(reset));  // open: en
  outputLogic outputlogic_1 (
    .s0(register_1_q[2]), .s1(register_1_q[1]), .s2(register_1_q[0]), .in1(dir[1]), .in0(dir[0]),
    .arrive(arrive), .hit(hit));
endmodule

module nextStateLogic (
  input  state0,
  input  state1,
  input  state2,
  input  in0,
  input  in1,
  output nState0,
  output nState1,
  output nState2
);

  wire and_1_out, and_2_out, and_3_out, and_4_out, and_5_out, and_6_out, and_7_out, and_8_out, and_9_out,
       and_10_out, not_1_out, not_2_out, not_3_out, not_4_out, not_5_out, not_6_out, not_7_out, not_8_out,
       not_9_out, not_10_out, not_11_out, not_12_out, not_13_out, not_14_out, not_15_out, not_16_out,
       not_17_out, not_18_out, not_19_out, not_20_out, not_21_out, not_22_out, not_23_out, not_24_out,
       not_25_out, not_26_out, not_27_out;

  not not_1 (not_1_out, state0);
  not not_2 (not_2_out, state2);
  not not_3 (not_3_out, in0);
  not not_4 (not_4_out, in1);
  not not_5 (not_5_out, state1);
  not not_6 (not_6_out, state2);
  not not_7 (not_7_out, in0);
  not not_8 (not_8_out, in1);
  not not_9 (not_9_out, state1);
  not not_10 (not_10_out, state2);
  not not_11 (not_11_out, state0);
  not not_12 (not_12_out, state1);
  not not_13 (not_13_out, state2);
  not not_14 (not_14_out, in0);
  not not_15 (not_15_out, in1);
  not not_16 (not_16_out, state0);
  not not_17 (not_17_out, state0);
  not not_18 (not_18_out, state1);
  not not_19 (not_19_out, state2);
  not not_20 (not_20_out, in1);
  not not_21 (not_21_out, state0);
  not not_22 (not_22_out, in0);
  not not_23 (not_23_out, state0);
  not not_24 (not_24_out, in1);
  not not_25 (not_25_out, state1);
  not not_26 (not_26_out, state2);
  not not_27 (not_27_out, in0);
  and and_1 (and_1_out, not_1_out, state1, not_2_out, not_3_out, not_4_out);
  and and_2 (and_2_out, state0, not_5_out, not_6_out, not_7_out, not_8_out);
  and and_3 (and_3_out, state0, not_9_out, not_10_out, in0, in1);
  and and_4 (and_4_out, not_11_out, not_12_out, not_13_out, not_14_out, not_15_out);
  and and_5 (and_5_out, not_16_out, state1, in1);
  and and_6 (and_6_out, not_17_out, state1, state2, in0);
  and and_7 (and_7_out, state0, not_18_out, not_19_out, in0, not_20_out);
  and and_8 (and_8_out, not_21_out, state1, not_22_out, in1);
  and and_9 (and_9_out, not_23_out, state1, state2, not_24_out);
  and and_10 (and_10_out, state0, not_25_out, not_26_out, not_27_out, in1);
  or or_1 (nState0, and_1_out, and_2_out, and_3_out);
  or or_2 (nState1, and_4_out, and_5_out, and_6_out, and_7_out);
  or or_3 (nState2, and_8_out, and_9_out, and_10_out);
endmodule

module outputLogic (
  input  s0,
  input  s1,
  input  s2,
  input  in1,
  input  in0,
  output arrive,
  output hit
);

  wire and_2_out, and_3_out, and_4_out, and_5_out, and_6_out, and_7_out, not_1_out, not_2_out, not_3_out,
       not_4_out, not_5_out, not_6_out, not_7_out, not_8_out, not_9_out, not_10_out, not_11_out, not_12_out,
       not_13_out;

  not not_1 (not_1_out, s0);
  not not_2 (not_2_out, s1);
  not not_3 (not_3_out, s0);
  not not_4 (not_4_out, s1);
  not not_5 (not_5_out, s2);
  not not_6 (not_6_out, s0);
  not not_7 (not_7_out, s1);
  not not_8 (not_8_out, s2);
  not not_9 (not_9_out, s2);
  not not_10 (not_10_out, in1);
  not not_11 (not_11_out, in0);
  not not_12 (not_12_out, in1);
  not not_13 (not_13_out, in0);
  and and_1 (arrive, not_1_out, not_2_out, s2);
  and and_2 (and_2_out, not_3_out, not_4_out, not_5_out, in0);
  and and_3 (and_3_out, not_6_out, not_7_out, not_8_out, in1);
  and and_4 (and_4_out, not_9_out, in1, in0);
  and and_5 (and_5_out, s1, s2, not_10_out, in0);
  and and_6 (and_6_out, s1, s2, in1, not_11_out);
  and and_7 (and_7_out, s0, not_12_out, not_13_out);
  or or_1 (hit, and_2_out, and_3_out, and_4_out, and_5_out, and_6_out, and_7_out);
endmodule

module test (
  input  in_1,
  output out_2,
  output out_3
);

  wire clock_1_out;
  wire [1:0] rom_1_data;
  wire [7:0] counter_1_q;

  Clock clock_1 (.out(clock_1_out));
  Counter counter_1 (.Q(counter_1_q), .clk(clock_1_out), .clr(in_1));  // open: load, D, count, carry
  navigation navigation_1 (.dir(rom_1_data), .clk(clock_1_out), .reset(in_1), .arrive(out_2), .hit(out_3));
  ROM #(.dataWidth(2)) rom_1 (.addr(counter_1_q), .data(rom_1_data));  // open: sel

  // Notes on the sheet:
  //   contents of rom_1 (hex, n*v repeats v):
  //   0 3 0 5*3 1 0 2 0 0 2 3 1 2 3 1 2 3 2 2 0 2 1 0 3 3 2 0 0 3
endmodule
