// Logisim project rgf.circ as structural Verilog: 2 circuits, main circuit grf
module grf (
  input  clk,
  input  reset,
  input  [31:0] WD,
  input  [4:0] A1,
  input  WE,
  input  [4:0] A2,
  input  [4:0] A3,
  output [31:0] RD1,
  output [31:0] RD2
);

  wire [31:0] data0, data1, data2, data3, data4, data5, data6, data7, data8, data9, data10, data11, data12,
       data13, data14, data15, data16, data17, data18, data19, data20, data21, data22, data23, data24,
       data25, data26, data27, data28, data29, data30, data31, r1, r2, r3, r4, r5, r6, r7, r8, r9, r10, r11,
       r12, r13, r14, r15, r16, r17, r18, r19, r20, r21, r22, r23, r24, r25, r26, r27, r28, r29, r30, r31;

  Multiplexer #(.select(5), .width(32), .enable("false")) multiplexer_1 (
    .in0({32{1'b0}}), .in1(r1), .in2(r2), .in3(r3), .in4(r4), .in5(r5), .in6(r6), .in7(r7), .in8(r8),
    .in9(r9), .in10(r10), .in11(r11), .in12(r12), .in13(r13), .in14(r14), .in15(r15), .in16(r16), .in17(r17),
    .in18(r18), .in19(r19), .in20(r20), .in21(r21), .in22(r22), .in23(r23), .in24(r24), .in25(r25),
    .in26(r26), .in27(r27), .in28(r28), .in29(r29), .in30(r30), .in31(r31), .out(RD1), .sel(A1));
  Register #(.width(32)) REG1 (.D(data1), .en(WE), .Q(r1), .clk(clk), .clr(reset));
  Register #(.width(32)) REG2 (.D(data2), .en(WE), .Q(r2), .clk(clk), .clr(reset));
  Register #(.width(32)) REG3 (.D(data3), .en(WE), .Q(r3), .clk(clk), .clr(reset));
  Register #(.width(32)) REG4 (.D(data4), .en(WE), .Q(r4), .clk(clk), .clr(reset));
  Register #(.width(32)) REG5 (.D(data5), .en(WE), .Q(r5), .clk(clk), .clr(reset));
  Register #(.width(32)) REG6 (.D(data6), .en(WE), .Q(r6), .clk(clk), .clr(reset));
  Register #(.width(32)) REG7 (.D(data7), .en(WE), .Q(r7), .clk(clk), .clr(reset));
  Register #(.width(32)) REG8 (.D(data8), .en(WE), .Q(r8), .clk(clk), .clr(reset));
  Register #(.width(32)) REG9 (.D(data9), .en(WE), .Q(r9), .clk(clk), .clr(reset));
  Register #(.width(32)) REG10 (.D(data10), .en(WE), .Q(r10), .clk(clk), .clr(reset));
  Register #(.width(32)) REG11 (.D(data11), .en(WE), .Q(r11), .clk(clk), .clr(reset));
  Register #(.width(32)) REG12 (.D(data12), .en(WE), .Q(r12), .clk(clk), .clr(reset));
  Register #(.width(32)) REG13 (.D(data13), .en(WE), .Q(r13), .clk(clk), .clr(reset));
  Register #(.width(32)) REG14 (.D(data14), .en(WE), .Q(r14), .clk(clk), .clr(reset));
  Register #(.width(32)) REG15 (.D(data15), .en(WE), .Q(r15), .clk(clk), .clr(reset));
  Register #(.width(32)) REG16 (.D(data16), .en(WE), .Q(r16), .clk(clk), .clr(reset));
  Register #(.width(32)) REG17 (.D(data17), .en(WE), .Q(r17), .clk(clk), .clr(reset));
  Register #(.width(32)) REG18 (.D(data18), .en(WE), .Q(r18), .clk(clk), .clr(reset));
  Register #(.width(32)) REG19 (.D(data19), .en(WE), .Q(r19), .clk(clk), .clr(reset));
  Register #(.width(32)) REG20 (.D(data20), .en(WE), .Q(r20), .clk(clk), .clr(reset));
  Register #(.width(32)) REG21 (.D(data21), .en(WE), .Q(r21), .clk(clk), .clr(reset));
  Register #(.width(32)) REG22 (.D(data22), .en(WE), .Q(r22), .clk(clk), .clr(reset));
  Register #(.width(32)) REG23 (.D(data23), .en(WE), .Q(r23), .clk(clk), .clr(reset));
  Register #(.width(32)) REG24 (.D(data24), .en(WE), .Q(r24), .clk(clk), .clr(reset));
  Register #(.width(32)) REG25 (.D(data25), .en(WE), .Q(r25), .clk(clk), .clr(reset));
  Register #(.width(32)) REG26 (.D(data26), .en(WE), .Q(r26), .clk(clk), .clr(reset));
  Register #(.width(32)) REG27 (.D(data27), .en(WE), .Q(r27), .clk(clk), .clr(reset));
  Register #(.width(32)) REG28 (.D(data28), .en(WE), .Q(r28), .clk(clk), .clr(reset));
  Register #(.width(32)) REG29 (.D(data29), .en(WE), .Q(r29), .clk(clk), .clr(reset));
  Register #(.width(32)) REG30 (.D(data30), .en(WE), .Q(r30), .clk(clk), .clr(reset));
  Register #(.width(32)) REG31 (.D(data31), .en(WE), .Q(r31), .clk(clk), .clr(reset));
  Multiplexer #(.select(5), .width(32), .enable("false")) multiplexer_2 (
    .in0({32{1'b0}}), .in1(r1), .in2(r2), .in3(r3), .in4(r4), .in5(r5), .in6(r6), .in7(r7), .in8(r8),
    .in9(r9), .in10(r10), .in11(r11), .in12(r12), .in13(r13), .in14(r14), .in15(r15), .in16(r16), .in17(r17),
    .in18(r18), .in19(r19), .in20(r20), .in21(r21), .in22(r22), .in23(r23), .in24(r24), .in25(r25),
    .in26(r26), .in27(r27), .in28(r28), .in29(r29), .in30(r30), .in31(r31), .out(RD2), .sel(A2));
  // Probe on WD
  Demultiplexer #(.select(5), .width(32), .tristate("true"), .enable("false")) demultiplexer_1 (
    .out0(data0), .out1(data1), .out2(data2), .out3(data3), .out4(data4), .out5(data5), .out6(data6),
    .out7(data7), .out8(data8), .out9(data9), .out10(data10), .out11(data11), .out12(data12), .out13(data13),
    .out14(data14), .out15(data15), .out16(data16), .out17(data17), .out18(data18), .out19(data19),
    .out20(data20), .out21(data21), .out22(data22), .out23(data23), .out24(data24), .out25(data25),
    .out26(data26), .out27(data27), .out28(data28), .out29(data29), .out30(data30), .out31(data31), .in(WD),
    .sel(A3));
endmodule

module test (
  input  in_1,
  input  in_2,
  input  in_3,
  input  in_4,
  input  [4:0] in_5,
  input  [4:0] in_6,
  input  [4:0] in_7,
  input  [31:0] in_8,
  output [31:0] out_9,
  output [31:0] out_10
);

  wire clock_1_out, clock_2_out, or_1_out;
  wire [7:0] counter_1_q;
  wire [16:0] rom_1_data;
  wire [31:0] grf_1_rd1, grf_1_rd2, rom_2_data;

  Counter counter_1 (.Q(counter_1_q), .clk(clock_1_out), .clr(in_1));  // open: load, D, count, carry
  Clock clock_1 (.out(clock_1_out));
  ROM #(.dataWidth(17)) rom_1 (.addr(counter_1_q), .data(rom_1_data));  // open: sel
  ROM #(.dataWidth(32)) rom_2 (.addr(counter_1_q), .data(rom_2_data));  // open: sel
  or or_1 (or_1_out, in_1, rom_1_data[0]);
  // Probe on grf_1_rd1
  grf grf_1 (
    .clk(in_4), .reset(in_3), .WD(in_8), .WE(in_2), .A1(in_5), .A2(in_6), .A3(in_7), .RD1(grf_1_rd1),
    .RD2(grf_1_rd2));
  // Probe on grf_1_rd2
  Clock clock_2 (.out(clock_2_out));
  grf grf_2 (
    .clk(clock_2_out), .reset(or_1_out), .WD(rom_2_data), .WE(rom_1_data[1]), .A1(rom_1_data[6:2]),
    .A2(rom_1_data[11:7]), .A3(rom_1_data[16:12]), .RD1(out_9), .RD2(out_10));

  // Notes on the sheet:
  //   contents of rom_1 (hex, n*v repeats v):
  //   5002 2400
  //   contents of rom_2 (hex, n*v repeats v):
  //   11 12 21
endmodule
