// Logisim project cpu.circ as structural Verilog: 14 circuits, main circuit main
module GRF (
  input  clk,
  input  reset,
  input  [31:0] WD,
  input  [4:0] A1,
  input  WE,
  input  [4:0] A2,
  input  [4:0] A3,
  output [31:0] RD1,
  output [31:0] RD2
);

  wire [31:0] data0, data1, data2, data3, data4, data5, data6, data7, data8, data9, data10, data11, data12,
       data13, data14, data15, data16, data17, data18, data19, data20, data21, data22, data23, data24,
       data25, data26, data27, data28, data29, data30, data31, r1, r2, r3, r4, r5, r6, r7, r8, r9, r10, r11,
       r12, r13, r14, r15, r16, r17, r18, r19, r20, r21, r22, r23, r24, r25, r26, r27, r28, r29, r30, r31;

  Multiplexer #(.select(5), .width(32), .enable("false")) multiplexer_1 (
    .in0({32{1'b0}}), .in1(r1), .in2(r2), .in3(r3), .in4(r4), .in5(r5), .in6(r6), .in7(r7), .in8(r8),
    .in9(r9), .in10(r10), .in11(r11), .in12(r12), .in13(r13), .in14(r14), .in15(r15), .in16(r16), .in17(r17),
    .in18(r18), .in19(r19), .in20(r20), .in21(r21), .in22(r22), .in23(r23), .in24(r24), .in25(r25),
    .in26(r26), .in27(r27), .in28(r28), .in29(r29), .in30(r30), .in31(r31), .out(RD1), .sel(A1));
  Register #(.width(32)) REG1 (.D(data1), .en(WE), .Q(r1), .clk(clk), .clr(reset));
  Register #(.width(32)) REG2 (.D(data2), .en(WE), .Q(r2), .clk(clk), .clr(reset));
  Register #(.width(32)) REG3 (.D(data3), .en(WE), .Q(r3), .clk(clk), .clr(reset));
  Register #(.width(32)) REG4 (.D(data4), .en(WE), .Q(r4), .clk(clk), .clr(reset));
  Register #(.width(32)) REG5 (.D(data5), .en(WE), .Q(r5), .clk(clk), .clr(reset));
  Register #(.width(32)) REG6 (.D(data6), .en(WE), .Q(r6), .clk(clk), .clr(reset));
  Register #(.width(32)) REG7 (.D(data7), .en(WE), .Q(r7), .clk(clk), .clr(reset));
  Register #(.width(32)) REG8 (.D(data8), .en(WE), .Q(r8), .clk(clk), .clr(reset));
  Register #(.width(32)) REG9 (.D(data9), .en(WE), .Q(r9), .clk(clk), .clr(reset));
  Register #(.width(32)) REG10 (.D(data10), .en(WE), .Q(r10), .clk(clk), .clr(reset));
  Register #(.width(32)) REG11 (.D(data11), .en(WE), .Q(r11), .clk(clk), .clr(reset));
  Register #(.width(32)) REG12 (.D(data12), .en(WE), .Q(r12), .clk(clk), .clr(reset));
  Register #(.width(32)) REG13 (.D(data13), .en(WE), .Q(r13), .clk(clk), .clr(reset));
  Register #(.width(32)) REG14 (.D(data14), .en(WE), .Q(r14), .clk(clk), .clr(reset));
  Register #(.width(32)) REG15 (.D(data15), .en(WE), .Q(r15), .clk(clk), .clr(reset));
  Multiplexer #(.select(5), .width(32), .enable("false")) multiplexer_2 (
    .in0({32{1'b0}}), .in1(r1), .in2(r2), .in3(r3), .in4(r4), .in5(r5), .in6(r6), .in7(r7), .in8(r8),
    .in9(r9), .in10(r10), .in11(r11), .in12(r12), .in13(r13), .in14(r14), .in15(r15), .in16(r16), .in17(r17),
    .in18(r18), .in19(r19), .in20(r20), .in21(r21), .in22(r22), .in23(r23), .in24(r24), .in25(r25),
    .in26(r26), .in27(r27), .in28(r28), .in29(r29), .in30(r30), .in31(r31), .out(RD2), .sel(A2));
  Register #(.width(32)) REG16 (.D(data16), .en(WE), .Q(r16), .clk(clk), .clr(reset));
  Register #(.width(32)) REG17 (.D(data17), .en(WE), .Q(r17), .clk(clk), .clr(reset));
  Register #(.width(32)) REG18 (.D(data18), .en(WE), .Q(r18), .clk(clk), .clr(reset));
  Register #(.width(32)) REG19 (.D(data19), .en(WE), .Q(r19), .clk(clk), .clr(reset));
  Register #(.width(32)) REG20 (.D(data20), .en(WE), .Q(r20), .clk(clk), .clr(reset));
  Register #(.width(32)) REG21 (.D(data21), .en(WE), .Q(r21), .clk(clk), .clr(reset));
  Register #(.width(32)) REG22 (.D(data22), .en(WE), .Q(r22), .clk(clk), .clr(reset));
  Register #(.width(32)) REG23 (.D(data23), .en(WE), .Q(r23), .clk(clk), .clr(reset));
  Register #(.width(32)) REG24 (.D(data24), .en(WE), .Q(r24), .clk(clk), .clr(reset));
  Register #(.width(32)) REG25 (.D(data25), .en(WE), .Q(r25), .clk(clk), .clr(reset));
  Register #(.width(32)) REG26 (.D(data26), .en(WE), .Q(r26), .clk(clk), .clr(reset));
  Register #(.width(32)) REG27 (.D(data27), .en(WE), .Q(r27), .clk(clk), .clr(reset));
  Register #(.width(32)) REG28 (.D(data28), .en(WE), .Q(r28), .clk(clk), .clr(reset));
  Register #(.width(32)) REG29 (.D(data29), .en(WE), .Q(r29), .clk(clk), .clr(reset));
  Register #(.width(32)) REG30 (.D(data30), .en(WE), .Q(r30), .clk(clk), .clr(reset));
  Register #(.width(32)) REG31 (.D(data31), .en(WE), .Q(r31), .clk(clk), .clr(reset));
  // Probe on WD
  Demultiplexer #(.select(5), .width(32), .tristate("true"), .enable("false")) demultiplexer_1 (
    .out0(data0), .out1(data1), .out2(data2), .out3(data3), .out4(data4), .out5(data5), .out6(data6),
    .out7(data7), .out8(data8), .out9(data9), .out10(data10), .out11(data11), .out12(data12), .out13(data13),
    .out14(data14), .out15(data15), .out16(data16), .out17(data17), .out18(data18), .out19(data19),
    .out20(data20), .out21(data21), .out22(data22), .out23(data23), .out24(data24), .out25(data25),
    .out26(data26), .out27(data27), .out28(data28), .out29(data29), .out30(data30), .out31(data31), .in(WD),
    .sel(A3));
endmodule

module main (
  input  rst,
  output [31:0] instr,
  output [31:0] pc,
  output regWE,
  output [4:0] REGaddr,
  output [31:0] REGdata,
  output DMWE,
  output [31:0] DMaddr,
  output [31:0] DMdata
);

  wire alu_1_out_5, ALUsrc, Branch, clk, DMRE, equal, extSignal, j, jal, jr, not_1_out;
  wire [1:0] RegData_t, RegDes;
  wire [2:0] ALUop;
  wire [4:0] rd, rs, rt, shamt;
  wire [8:0] ReadAddr;
  wire [15:0] imm;
  wire [25:0] j_addr;
  wire [31:0] ExtendedImm, MemoData, multiplexer_1_out, nimm_1_imm, PC_4, RD1, shifter_1_out;

  Clock clock_1 (.out(clk));
  not not_1 (not_1_out, extSignal);
  Nimm nimm_1 (.j(j), .jr(jr), .in_3(ExtendedImm), .in_4(instr), .in_5(RD1), .imm(nimm_1_imm));
  Controller controller_1 (
    .instr(instr), .RegDes(RegDes), .ALUsrc(ALUsrc), .ALUop(ALUop), .DMRE(DMRE), .DMWE(DMWE),
    .Branch(Branch), .j(j), .unsignedExt(extSignal), .RegWE(regWE), .RegData(RegData_t), .jal(jal), .jr(jr));
  EXT ext_1 (.in(imm), .op(not_1_out), .out(ExtendedImm));
  IFU ifu_1 (
    .clk(clk), .reset(rst), .beq(Branch), .eq(equal), .imm32(nimm_1_imm), .instr32(instr), .j(j), .PC(pc),
    .PC_4(PC_4), .jr(jr));
  // Probe on instr
  Splitter splitter_1 (
    .instr(instr), .rs(rs), .rt(rt), .rd(rd), .shamt(shamt), .imm(imm), .j_addr(j_addr));  // open: op, funct
  Multiplexer #(.width(32), .enable("false")) multiplexer_1 (
    .in0(ExtendedImm), .in1(DMdata), .out(multiplexer_1_out), .sel(ALUsrc));
  Multiplexer #(.select(2), .width(5), .enable("false")) multiplexer_2 (
    .in0(rt), .in1(rd), .in3({5{1'b1}}), .out(REGaddr), .sel(RegDes));  // open: in2
  Multiplexer #(.select(2), .width(32), .enable("false")) multiplexer_3 (
    .in0(MemoData), .in1(DMaddr), .in3(PC_4), .out(REGdata), .sel(RegData_t));  // open: in2
  ALU alu_1 (.in1(RD1), .in2(multiplexer_1_out), .op(ALUop), .ans(DMaddr), .out_5(alu_1_out_5));
  and and_1 (equal, Branch, alu_1_out_5);
  Shifter #(.width(32), .shift("lr")) shifter_1 (.in(DMaddr), .\dist (5'b00010), .out(shifter_1_out));
  DM dm_1 (.clk(clk), .rst(rst), .WE(DMWE), .load(DMRE), .data(DMdata), .addr(ReadAddr), .out_7(MemoData));
  GRF grf_1 (.clk(clk), .reset(rst), .WD(REGdata), .WE(regWE), .A1(rs), .A2(rt), .A3(REGaddr), .RD1(RD1), .RD2(DMdata));
  Bit_Extender #(.in_width(32), .out_width(9)) bit_extender_1 (.in(shifter_1_out), .out(ReadAddr));

  // Other names for the same wires on the sheet: ALUresult[31:0] = DMaddr; RegData_out[31:0] = REGdata;
  //   RegSW[31:0] = DMdata
endmodule

module IFU (
  input  clk,
  input  reset,
  input  beq,
  input  eq,
  input  j,
  input  jr,
  input  [31:0] imm32,
  output [31:0] instr32,
  output [31:0] PC,
  output [31:0] PC_4
);

  wire [31:0] curPC, npc_1_nextpc, PC_4_t;

  NPC npc_1 (
    .beq(beq), .eq(eq), .j(j), .imm(imm32), .curPC(curPC), .nextPC(npc_1_nextpc), .curPC_4(PC_4_t), .jr(jr));  // open: b_PC, j_PC
  // Probe on npc_1_nextpc
  // Probe on curPC
  Counter #(.width(32), .max('hffffffff)) counter_1 (
    .load(1'b1), .D(npc_1_nextpc), .count(1'b0), .Q(curPC), .clk(clk), .clr(reset));  // open: carry
  ROM #(.addrWidth(12), .dataWidth(32)) rom_1 (.addr(curPC[13:2]), .data(instr32));  // open: sel
  Adder #(.width(32)) adder_1 (.a(curPC), .b(32'h3000), .out(PC));  // open: cin, cout
  Adder #(.width(32)) adder_2 (.a(PC_4_t), .b(32'h3000), .out(PC_4));  // open: cin, cout

  // Other names for the same wires on the sheet: rst = reset

  // Notes on the sheet:
  //   contents of rom_1 (hex, n*v repeats v):
  //   4*0 3e00008 0 0 8ea1003c 1370fff9 1f48820 0 0 2b46020 132cfff4 0 0 0 3046020 3c12f641 346a822
  //   36c2bcbb 0 2653022 2aa6022 3c0ff851 1266fffb 3c0c4c15 0 1bac820 0 1057fff6 0 0 ae7b0070 0 1028022 0
  //   26f5820 8d78005c 3434acd3 0 2ba2020 2848820 0 0 8df90000 0 20bb820 0 34f414f4 0 0 ae300028 1c2b020 0
  //   8cd1003c 0 3585820 1129820 1205ffd9 1367ffc5 0 afd020 0 0 2efa022 0 0 2771822 2d53820 0 0 0 1107822
  //   a2d022 8d57007c 1169ffc8 26d1822 1758022 1154ffc1 0 0 0 262c822 0 2a35022 2d72820 134effe3 1276ffeb
  //   0 1275820 1841820 2193822 0 0 24d8822 2ee2820 1ec4822 0 0 3c10e4a1 12c5022 0 36c6a5be 3c0dc9e5
  //   367d020 2e74822 12e6020 0 21a4020 aec20030 0 0 2f07822 10c1ffd1 0 35b2020 aee30044 ec8822 8f110058
  //   398020 3c14cf90 130cffc9 12b3022 1aa4820 0 2323020 10d5022 0 0 508822 0 3c0fd93e 2220820 0 0 1902822
  //   8c570064 376aa29f 0 1d89820 2375022 10f1ff86 0 0 0 26d1820 8ed90078 377a29d3 3c0110c0 3c027cda
  //   1327020 195c822 ae8a0038 14c9020 16e3820 0 0 0 34010001 1020fffe 8000c9f
endmodule

module EXT (
  input  [15:0] in,
  input  op,
  output [31:0] out
);

  wire [31:0] bit_extender_1_out, bit_extender_2_out;

  assign bit_extender_1_out = {{16{1'b0}}, in};  // Bit_Extender bit_extender_1
  assign bit_extender_2_out = {{16{in[15]}}, in};  // Bit_Extender bit_extender_2
  Multiplexer #(.width(32), .enable("false")) multiplexer_1 (
    .in0(bit_extender_1_out), .in1(bit_extender_2_out), .out(out), .sel(op));
endmodule

module Splitter (
  input  [31:0] instr,
  output [5:0] op,
  output [4:0] rs,
  output [4:0] rt,
  output [4:0] rd,
  output [4:0] shamt,
  output [5:0] funct,
  output [15:0] imm,
  output [25:0] j_addr
);


  assign funct = instr[5:0];
  assign imm = instr[15:0];
  assign j_addr = instr[25:0];
  assign op = instr[31:26];
  assign rd = instr[15:11];
  assign rs = instr[25:21];
  assign rt = instr[20:16];
  assign shamt = instr[10:6];

  // Other names for the same wires on the sheet: op_code[5:0] = instr[31:26]
endmodule

module DM (
  input  clk,
  input  rst,
  input  WE,
  input  load,
  input  [31:0] data,
  input  [8:0] addr,
  output [31:0] out_7
);

  RAM #(.addrWidth(9), .dataWidth(32), .bus("separate")) ram_1 (
    .addr(addr), .din(data), .data(out_7), .str(WE), .clk(clk), .ld(load), .clr(rst));  // open: sel
endmodule

module NPC (
  input  j,
  input  beq,
  input  eq,
  input  [31:0] imm,
  input  [31:0] curPC,
  input  jr,
  output [31:0] nextPC,
  output [31:0] curPC_4,
  output [31:0] b_PC,
  output [31:0] j_PC
);

  wire b;
  wire [15:0] shifter_1_out;
  wire [27:0] bit_extender_1_out, shifter_2_out;
  wire [31:0] bit_extender_2_out, jr_PC, multiplexer_1_out, multiplexer_2_out;

  and and_1 (b, beq, eq);
  Shifter #(.width(16)) shifter_1 (.in(imm[15:0]), .\dist (4'b0010), .out(shifter_1_out));
  assign bit_extender_1_out = {{2{imm[25]}}, imm[25:0]};  // Bit_Extender bit_extender_1
  assign bit_extender_2_out = {{16{shifter_1_out[15]}}, shifter_1_out};  // Bit_Extender bit_extender_2
  Shifter #(.width(28)) shifter_2 (.in(bit_extender_1_out), .\dist (5'b00010), .out(shifter_2_out));
  Adder #(.width(32)) adder_1 (.a(curPC), .b(32'h4), .out(curPC_4));  // open: cin, cout
  Adder #(.width(32)) adder_2 (.a(bit_extender_2_out), .b(curPC_4), .out(b_PC));  // open: cin, cout
  Subtractor #(.width(32)) subtractor_1 (.a(imm), .b(32'h3000), .out(jr_PC));  // open: bin, bout
  Subtractor #(.width(32)) subtractor_2 (
    .a({curPC[31:28], shifter_2_out}), .b(32'h3000), .out(j_PC));  // open: bin, bout
  // Probe on multiplexer_1_out
  Multiplexer #(.width(32), .enable("false")) multiplexer_1 (
    .in0(curPC_4), .in1(b_PC), .out(multiplexer_1_out), .sel(b));
  Multiplexer #(.width(32), .enable("false")) multiplexer_2 (
    .in0(multiplexer_1_out), .in1(j_PC), .out(multiplexer_2_out), .sel(j));
  Multiplexer #(.width(32), .enable("false")) multiplexer_3 (
    .in0(multiplexer_2_out), .in1(jr_PC), .out(nextPC), .sel(jr));
endmodule

module ALU (
  input  [31:0] in1,
  input  [31:0] in2,
  input  [2:0] op,
  output [31:0] ans,
  output out_5
);

  wire addu, \and , \or , subu;
  wire [31:0] adder_1_out, and_1_out, multiplexer_1_out, negator_1_out, or_1_out, shifter_1_out;

  Decoder #(.select(3), .enable("false")) decoder_1 (
    .out0(addu), .out1(subu), .out2(\and ), .out3(\or ), .sel(op));  // open: out4, out5, out6, out7
  Negator #(.width(32)) negator_1 (.in(in2), .out(negator_1_out));
  Multiplexer #(.width(32), .enable("false")) multiplexer_1 (
    .in0(in2), .in1(negator_1_out), .out(multiplexer_1_out), .sel(subu));
  assign and_1_out = in1 & in2;  // AND_Gate and_1, 32 bits wide
  Shifter #(.width(32)) shifter_1 (.in(in2), .\dist (5'b10000), .out(shifter_1_out));
  Adder #(.width(32)) adder_1 (.a(in1), .b(multiplexer_1_out), .out(adder_1_out));  // open: cin, cout
  assign or_1_out = in1 | in2;  // OR_Gate or_1, 32 bits wide
  Multiplexer #(.select(3), .width(32), .enable("false")) multiplexer_2 (
    .in0(adder_1_out), .in1(adder_1_out), .in2(and_1_out), .in3(or_1_out), .in4(shifter_1_out), .out(ans),
    .sel(op));  // open: in5, in6, in7
  Comparator #(.width(32)) comparator_1 (.a(ans), .b({32{1'b0}}), .eq(out_5));  // open: gt, lt
endmodule

module Controller (
  input  [31:0] instr,
  output unsignedExt,
  output RegWE,
  output [1:0] RegData,
  output [1:0] RegDes,
  output ALUsrc,
  output DMRE,
  output DMWE,
  output [2:0] ALUop,
  output Branch,
  output j,
  output jr,
  output jal
);

  wire aludec_1_jr, and_1_out, checkjb_1_j;
  wire [2:0] maindecoder_1_alu1;
  wire [5:0] splitter_1_funct, splitter_1_op;

  Splitter splitter_1 (
    .instr(instr), .op(splitter_1_op), .funct(splitter_1_funct));  // open: rs, rt, rd, shamt, imm, j_addr
  // Probe on instr
  checkJB checkjb_1 (
    .in5(splitter_1_op[5]), .in4(splitter_1_op[4]), .in3(splitter_1_op[3]), .in2(splitter_1_op[2]),
    .in1(splitter_1_op[1]), .in0(splitter_1_op[0]), .branch(Branch), .j(checkjb_1_j), .jal(jal));
  and and_1 (and_1_out, ~splitter_1_op[5], ~splitter_1_op[4], ~splitter_1_op[3], ~splitter_1_op[2], ~splitter_1_op[1], ~splitter_1_op[0]);  // AND_Gate
  MainDecoder maindecoder_1 (
    .in5(splitter_1_op[5]), .unsignedExt(unsignedExt), .in4(splitter_1_op[4]), .in3(splitter_1_op[3]),
    .in2(splitter_1_op[2]), .in1(splitter_1_op[1]), .in0(splitter_1_op[0]), .RegWE(RegWE),
    .RegData(RegData[0]), .RegData1(RegData[1]), .RegDes(RegDes[0]), .RegDes1(RegDes[1]), .ALUsrc(ALUsrc),
    .DMRE(DMRE), .DMWE(DMWE), .alu1(maindecoder_1_alu1[0]), .alu2(maindecoder_1_alu1[1]),
    .alu3(maindecoder_1_alu1[2]));
  ALUDec aludec_1 (.ALU(maindecoder_1_alu1), .funct(splitter_1_funct), .ALUop(ALUop), .jr(aludec_1_jr));
  and and_2 (jr, aludec_1_jr, and_1_out);
  or or_1 (j, checkjb_1_j, jal, jr);
endmodule

module MainDecoder (
  input  in5,
  input  in4,
  input  in3,
  input  in2,
  input  in1,
  input  in0,
  output unsignedExt,
  output RegWE,
  output RegData,
  output RegData1,
  output RegDes,
  output RegDes1,
  output ALUsrc,
  output DMRE,
  output DMWE,
  output alu1,
  output alu2,
  output alu3
);

  wire and_2_out, and_3_out, and_4_out, and_5_out, and_6_out, and_7_out, and_8_out, and_9_out, and_10_out,
       and_11_out, and_12_out, and_13_out, and_15_out, and_16_out, and_17_out, and_18_out, and_19_out,
       and_20_out, and_24_out, and_25_out, and_26_out, and_27_out, and_28_out, and_29_out, and_30_out,
       and_31_out, and_32_out, and_33_out, and_34_out, and_35_out, and_36_out, not_1_out, not_2_out,
       not_3_out, not_4_out, not_5_out, not_6_out, not_7_out, not_8_out, not_9_out, not_10_out, not_11_out,
       not_12_out, not_13_out, not_14_out, not_15_out, not_16_out, not_17_out, not_18_out, not_19_out,
       not_20_out, not_21_out, not_22_out, not_23_out, not_24_out, not_25_out, not_26_out, not_27_out,
       not_28_out, not_29_out, not_30_out, not_31_out, not_32_out, not_33_out, not_34_out, not_35_out,
       not_36_out, not_37_out, not_38_out, not_39_out, not_40_out, not_41_out, not_42_out, not_43_out,
       not_44_out, not_45_out, not_46_out, not_47_out, not_48_out, not_49_out, not_50_out, not_51_out,
       not_52_out, not_53_out, not_54_out, not_55_out, not_56_out, not_57_out, not_58_out, not_59_out,
       not_60_out, not_61_out, not_62_out, not_63_out, not_64_out, not_65_out, not_66_out, not_67_out,
       not_68_out;

  not not_1 (not_1_out, in5);
  not not_2 (not_2_out, in4);
  not not_3 (not_3_out, in3);
  not not_4 (not_4_out, in2);
  not not_5 (not_5_out, in0);
  not not_6 (not_6_out, in3);
  not not_7 (not_7_out, in5);
  not not_8 (not_8_out, in4);
  not not_9 (not_9_out, in3);
  not not_10 (not_10_out, in3);
  not not_11 (not_11_out, in1);
  not not_12 (not_12_out, in0);
  not not_13 (not_13_out, in5);
  not not_14 (not_14_out, in4);
  not not_15 (not_15_out, in3);
  not not_16 (not_16_out, in2);
  not not_17 (not_17_out, in1);
  not not_18 (not_18_out, in1);
  not not_19 (not_19_out, in5);
  not not_20 (not_20_out, in4);
  not not_21 (not_21_out, in1);
  not not_22 (not_22_out, in1);
  not not_23 (not_23_out, in5);
  not not_24 (not_24_out, in4);
  not not_25 (not_25_out, in3);
  not not_26 (not_26_out, in2);
  not not_27 (not_27_out, in1);
  not not_28 (not_28_out, in0);
  not not_29 (not_29_out, in5);
  not not_30 (not_30_out, in4);
  not not_31 (not_31_out, in3);
  not not_32 (not_32_out, in2);
  not not_33 (not_33_out, in3);
  not not_34 (not_34_out, in1);
  not not_35 (not_35_out, in2);
  not not_36 (not_36_out, in1);
  not not_37 (not_37_out, in1);
  not not_38 (not_38_out, in1);
  not not_39 (not_39_out, in5);
  not not_40 (not_40_out, in4);
  not not_41 (not_41_out, in3);
  not not_42 (not_42_out, in2);
  not not_43 (not_43_out, in5);
  not not_44 (not_44_out, in4);
  not not_45 (not_45_out, in3);
  not not_46 (not_46_out, in1);
  not not_47 (not_47_out, in0);
  not not_48 (not_48_out, in3);
  not not_49 (not_49_out, in2);
  not not_50 (not_50_out, in0);
  not not_51 (not_51_out, in1);
  not not_52 (not_52_out, in0);
  not not_53 (not_53_out, in1);
  not not_54 (not_54_out, in1);
  not not_55 (not_55_out, in1);
  not not_56 (not_56_out, in1);
  not not_57 (not_57_out, in5);
  not not_58 (not_58_out, in4);
  not not_59 (not_59_out, in3);
  not not_60 (not_60_out, in2);
  not not_61 (not_61_out, in1);
  not not_62 (not_62_out, in0);
  not not_63 (not_63_out, in5);
  not not_64 (not_64_out, in4);
  not not_65 (not_65_out, in1);
  not not_66 (not_66_out, in2);
  not not_67 (not_67_out, in0);
  not not_68 (not_68_out, in5);
  and and_1 (unsignedExt, not_1_out, not_2_out, in3, in2, in0);
  and and_2 (and_2_out, not_3_out, not_4_out, not_5_out);
  and and_3 (and_3_out, not_6_out, in1);
  and and_4 (and_4_out, not_7_out, not_8_out, in2, in0);
  and and_5 (and_5_out, in4, not_9_out);
  and and_6 (and_6_out, in5, not_10_out);
  and and_7 (and_7_out, not_11_out, not_12_out);
  and and_8 (and_8_out, not_13_out, not_14_out, not_15_out, not_16_out, in1, in0);
  and and_9 (and_9_out, in2, not_17_out);
  and and_10 (and_10_out, in3, not_18_out);
  and and_11 (and_11_out, not_19_out, not_20_out, in3, in2, in0);
  and and_12 (and_12_out, in4, not_21_out);
  and and_13 (and_13_out, in5, not_22_out);
  and and_14 (RegData1, not_23_out, not_24_out, not_25_out, not_26_out, in1, in0);
  and and_15 (and_15_out, not_27_out, not_28_out);
  and and_16 (and_16_out, not_29_out, not_30_out, not_31_out, not_32_out, in1, in0);
  and and_17 (and_17_out, not_33_out, in2, not_34_out);
  and and_18 (and_18_out, in3, not_35_out, not_36_out);
  and and_19 (and_19_out, in4, not_37_out);
  and and_20 (and_20_out, in5, not_38_out);
  and and_21 (RegDes1, not_39_out, not_40_out, not_41_out, not_42_out, in1, in0);
  and and_22 (ALUsrc, not_43_out, not_44_out, not_45_out, not_46_out, not_47_out);
  and and_23 (DMRE, not_48_out, in1);
  and and_24 (and_24_out, in3, not_49_out);
  and and_25 (and_25_out, in3, not_50_out);
  and and_26 (and_26_out, in4, in3);
  and and_27 (and_27_out, in5, in3);
  and and_28 (and_28_out, not_51_out, not_52_out);
  and and_29 (and_29_out, in2, not_53_out);
  and and_30 (and_30_out, in3, not_54_out);
  and and_31 (and_31_out, in4, not_55_out);
  and and_32 (and_32_out, in5, not_56_out);
  and and_33 (and_33_out, not_57_out, not_58_out, not_59_out, not_60_out, not_61_out, not_62_out);
  and and_34 (and_34_out, not_63_out, not_64_out, in3, in2, not_65_out, in0);
  and and_35 (and_35_out, not_66_out, not_67_out);
  and and_36 (and_36_out, not_68_out, in1);
  or or_1 (RegWE, and_2_out, and_3_out, and_4_out, and_5_out, and_6_out);
  or or_2 (RegData, and_7_out, and_8_out, and_9_out, and_10_out, and_11_out, and_12_out, and_13_out);
  or or_3 (RegDes, and_15_out, and_16_out, and_17_out, and_18_out, and_19_out, and_20_out);
  or or_4 (DMWE, and_24_out, and_25_out, and_26_out, and_27_out);
  or or_5 (alu1, and_28_out, and_29_out, and_30_out, and_31_out, and_32_out);
  or or_6 (alu2, and_33_out, and_34_out);
  or or_7 (alu3, and_35_out, and_36_out);
endmodule

module ALUDec (
  input  [2:0] ALU,
  input  [5:0] funct,
  output [2:0] ALUop,
  output jr
);

  wire and_1_out;
  wire [2:0] functdec_1_alu0;

  and and_1 (and_1_out, ALU[0], ALU[1], ALU[2]);
  functDec functdec_1 (
    .in5(funct[5]), .in4(funct[4]), .in3(funct[3]), .in2(funct[2]), .in1(funct[1]), .in0(funct[0]),
    .alu2(functdec_1_alu0[2]), .alu1(functdec_1_alu0[1]), .alu0(functdec_1_alu0[0]), .jal(jr));
  Multiplexer #(.width(3), .enable("false")) multiplexer_1 (
    .in0(ALU), .in1(functdec_1_alu0), .out(ALUop), .sel(and_1_out));
endmodule

module functDec (
  input  in5,
  input  in4,
  input  in3,
  input  in2,
  input  in1,
  input  in0,
  output alu2,
  output alu1,
  output alu0,
  output jal
);

  wire not_1_out, not_2_out, not_3_out, not_4_out, not_5_out;

  not not_1 (not_1_out, in5);
  not not_2 (not_2_out, in4);
  not not_3 (not_3_out, in2);
  not not_4 (not_4_out, in1);
  not not_5 (not_5_out, in0);
  and and_1 (jal, not_1_out, not_2_out, in3, not_3_out, not_4_out, not_5_out);

  assign alu0 = in1;
  assign alu1 = 1'b0;
  assign alu2 = 1'b0;
endmodule

module checkJB (
  input  in5,
  input  in4,
  input  in3,
  input  in2,
  input  in1,
  input  in0,
  output branch,
  output j,
  output jal
);

  wire not_1_out, not_2_out, not_3_out, not_4_out, not_5_out, not_6_out, not_7_out, not_8_out, not_9_out,
       not_10_out, not_11_out, not_12_out, not_13_out, not_14_out;

  not not_1 (not_1_out, in5);
  not not_2 (not_2_out, in4);
  not not_3 (not_3_out, in3);
  not not_4 (not_4_out, in1);
  not not_5 (not_5_out, in0);
  not not_6 (not_6_out, in5);
  not not_7 (not_7_out, in4);
  not not_8 (not_8_out, in3);
  not not_9 (not_9_out, in2);
  not not_10 (not_10_out, in0);
  not not_11 (not_11_out, in5);
  not not_12 (not_12_out, in4);
  not not_13 (not_13_out, in3);
  not not_14 (not_14_out, in2);
  and and_1 (branch, not_1_out, not_2_out, not_3_out, in2, not_4_out, not_5_out);
  and and_2 (j, not_6_out, not_7_out, not_8_out, not_9_out, in1, not_10_out);
  and and_3 (jal, not_11_out, not_12_out, not_13_out, not_14_out, in1, in0);
endmodule

module Nimm (
  input  j,
  input  jr,
  input  [31:0] in_3,
  input  [31:0] in_4,
  input  [31:0] in_5,
  output [31:0] imm
);

  wire [31:0] multiplexer_1_out;

  Multiplexer #(.width(32), .enable("false")) multiplexer_1 (.in0(in_3), .in1(in_4), .out(multiplexer_1_out), .sel(j));
  Multiplexer #(.width(32), .enable("false")) multiplexer_2 (.in0(multiplexer_1_out), .in1(in_5), .out(imm), .sel(jr));

  // Other names for the same wires on the sheet: ExtendedImm[31:0] = in_3; instr[31:0] = in_4; RD1[31:0] = in_5
endmodule
