// Logisim project logisim_fibo.circ as structural Verilog: 3 circuits, main circuit main
module main (
  input  [2:0] in_1,
  input  in_2,
  output [3:0] out_3
);

  wire clock_1_out, counter_1_freeze;

  // Probe on counter_1_freeze
  counter counter_1 (.\freeze信号 (in_1), .rst(in_2), .clk(clock_1_out), .freeze(counter_1_freeze));
  Clock clock_1 (.out(clock_1_out));
  register register_1 (.freeze(counter_1_freeze), .clk(clock_1_out), .rst(in_2), .out_4(out_3));
endmodule

module counter (
  input  [2:0] \freeze信号 ,
  input  rst,
  input  clk,
  output freeze
);

  wire multiplexer_1_out;
  wire [2:0] counter_1_q;

  Counter #(.width(3), .max('h7), .ongoal("stay")) counter_1 (
    .Q(counter_1_q), .clk(multiplexer_1_out), .clr(rst));  // open: load, D, count, carry
  Multiplexer multiplexer_1 (.in0(clk), .out(multiplexer_1_out), .sel(freeze));  // open: in1, en
  Comparator #(.width(3)) comparator_1 (.a(\freeze信号 ), .b(counter_1_q), .eq(freeze));  // open: gt, lt

  // Notes on the sheet:
  //   counter接受输入数据，最后发出
endmodule

module register (
  input  freeze,
  input  clk,
  input  rst,
  output [3:0] out_4
);

  wire comparator_1_eq, freeze_n;
  wire [3:0] adder_1_out, demultiplexer_1_out1, now_q, pre_q;

  not not_1 (freeze_n, freeze);
  Register #(.width(4)) pre (.D(now_q), .en(freeze_n), .Q(pre_q), .clk(clk), .clr(rst));
  Register #(.width(4)) now (.D(adder_1_out), .en(freeze_n), .Q(now_q), .clk(clk), .clr(rst));
  Comparator #(.width(4)) comparator_1 (.a(4'b0000), .b(now_q), .eq(comparator_1_eq));  // open: gt, lt
  Demultiplexer #(.width(4)) demultiplexer_1 (
    .out0(out_4), .out1(demultiplexer_1_out1), .in(now_q), .sel(freeze_n));  // open: en
  Adder #(.width(4)) adder_1 (
    .a(pre_q), .b(demultiplexer_1_out1), .out(adder_1_out), .cin(comparator_1_eq));  // open: cout
endmodule
