// Logisim project swap.circ as structural Verilog: 3 circuits, main circuit 1bit_swap
module _1bit_swap (
  input  S,
  input  I1,
  input  I2,
  output O1,
  output O2
);

  wire and_1_out, and_2_out, and_3_out, and_4_out, not_1_out;

  not not_1 (not_1_out, S);
  and and_1 (and_1_out, not_1_out, I1);
  and and_2 (and_2_out, not_1_out, I2);
  and and_3 (and_3_out, S, I1);
  and and_4 (and_4_out, S, I2);
  or or_1 (O1, and_1_out, and_4_out);
  or or_2 (O2, and_2_out, and_3_out);
endmodule

module _4bit_swap (
  input  in_1,
  input  [3:0] in1,
  input  [3:0] in2,
  output [3:0] out1,
  output [3:0] out2
);

  _1bit_swap u_1bit_swap_1 (.I1(in1[0]), .I2(in2[0]), .O1(out1[0]), .O2(out2[0]), .S(in_1));
  _1bit_swap u_1bit_swap_2 (.I1(in1[1]), .I2(in2[1]), .O1(out1[1]), .O2(out2[1]), .S(in_1));
  _1bit_swap u_1bit_swap_3 (.I1(in1[2]), .I2(in2[2]), .O1(out1[2]), .O2(out2[2]), .S(in_1));
  _1bit_swap u_1bit_swap_4 (.I1(in1[3]), .I2(in2[3]), .O1(out1[3]), .O2(out2[3]), .S(in_1));
endmodule

module _4bit_sort (
  input  [3:0] in1,
  input  [3:0] in2,
  input  [3:0] in3,
  input  [3:0] in4,
  output [3:0] out1,
  output [3:0] out4,
  output [3:0] out2,
  output [3:0] out3
);

  wire comparator_1_gt, comparator_2_gt, comparator_3_gt, comparator_4_gt, comparator_5_gt;
  wire [3:0] n4bit_swap_1_out1, n4bit_swap_1_out2, n4bit_swap_2_out1, n4bit_swap_2_out2, n4bit_swap_3_out2,
       n4bit_swap_4_out1;

  Comparator #(.width(4), .mode("unsigned")) comparator_1 (.a(in1), .b(in2), .gt(comparator_1_gt));  // open: eq, lt
  Comparator #(.width(4), .mode("unsigned")) comparator_2 (.a(in3), .b(in4), .gt(comparator_2_gt));  // open: eq, lt
  _4bit_swap u_4bit_swap_1 (
    .in_1(comparator_1_gt), .in1(in1), .in2(in2), .out1(n4bit_swap_1_out1), .out2(n4bit_swap_1_out2));
  _4bit_swap u_4bit_swap_2 (
    .in_1(comparator_2_gt), .in1(in3), .in2(in4), .out1(n4bit_swap_2_out1), .out2(n4bit_swap_2_out2));
  Comparator #(.width(4), .mode("unsigned")) comparator_3 (
    .a(n4bit_swap_1_out1), .b(n4bit_swap_2_out1), .gt(comparator_3_gt));  // open: eq, lt
  Comparator #(.width(4), .mode("unsigned")) comparator_4 (
    .a(n4bit_swap_1_out2), .b(n4bit_swap_2_out2), .gt(comparator_4_gt));  // open: eq, lt
  _4bit_swap u_4bit_swap_3 (
    .in_1(comparator_3_gt), .in1(n4bit_swap_1_out1), .in2(n4bit_swap_2_out1), .out1(out1),
    .out2(n4bit_swap_3_out2));
  _4bit_swap u_4bit_swap_4 (
    .in_1(comparator_4_gt), .in1(n4bit_swap_1_out2), .in2(n4bit_swap_2_out2), .out1(n4bit_swap_4_out1),
    .out2(out4));
  Comparator #(.width(4), .mode("unsigned")) comparator_5 (
    .a(n4bit_swap_3_out2), .b(n4bit_swap_4_out1), .gt(comparator_5_gt));  // open: eq, lt
  _4bit_swap u_4bit_swap_5 (
    .in_1(comparator_5_gt), .in1(n4bit_swap_3_out2), .in2(n4bit_swap_4_out1), .out1(out2), .out2(out3));
endmodule
